# Fritzing sketch LIDAR_circuit (saved by Fritzing 0.9.3b)
breadboards: 2

parts:
  Part1 = Arduino Nano (Rev3.0)
  Azimuth = Basic Servo
  Altitude = Basic Servo
  C2 = Electrolytic Capacitor [capacitance=680µF package="300 mil [THT, electrolytic]"]
  Part2 = LIDAR-Lite
  J1 = 6 circuit slip ring

nets:
  GND: Part1.GND, Azimuth.gnd, Altitude.gnd, C2.-, Part2.GND, J1.pin_2#1, J1.pin_7
  N1: Part1.D9, Altitude.pulse, J1.pin_2#2, J1.pin_8
  N2: Part1.D10, Azimuth.pulse
  5V: Part1.5V, Azimuth.vcc, Altitude.vcc, C2.+, Part2.5V, J1.pin_3, J1.pin_9
  N3: Part1.A5, Part2.SCL, J1.pin_5, J1.pin_11
  N4: Part1.A4, Part2.SDA, J1.pin_4, J1.pin_10
  N5: J1.pin1, J1.pin_6

custom parts:
  LIDAR-Lite: PulsedLight LIDAR-Lite Sensor
  6 circuit slip ring: A 300 rpm 6 circuit 2A Slip Ring unit (connects a rotating part on top to wires on the bottom that don't rotate). Bigger (and much more expensive > $20 against $3.50 for these) have been available for a while, but these are the first small cheap ones that I have seen. Available from Ebay (search for "6 circuit slip ring" to find them). Outer flange is 24mm, inner body 12.5mm.
